// Logisim project ULA.circ as structural Verilog: 35 circuits, main circuit meiosomador
module meiosomador (
  input  in_1,
  input  in_2,
  output out_3,
  output out_4
);

  xor Soma (out_3, in_1, in_2);
  and Carry_In (out_4, in_1, in_2);
endmodule

module somadorcompleto (
  input  Cin,
  input  A,
  input  B,
  output \Saída_Soma ,
  output Cout
);

  wire A___B_out, A___Cin_out, B__Cin_out, Soma_out;

  xor Soma (Soma_out, A, B);
  and A___B (A___B_out, A, B);
  and A___Cin (A___Cin_out, A, Cin);
  and B__Cin (B__Cin_out, B, Cin);
  xor plus_Cin (\Saída_Soma , Cin, Soma_out);
  or Out (Cout, A___B_out, A___Cin_out, B__Cin_out);
endmodule

module MUX32 (
  input  E0,
  input  E1,
  input  E2,
  input  E3,
  input  E4,
  input  E5,
  input  E6,
  input  E7,
  input  E8,
  input  E9,
  input  E10,
  input  E11,
  input  E12,
  input  E13,
  input  E14,
  input  E15,
  input  E16,
  input  E17,
  input  E18,
  input  E19,
  input  E20,
  input  E21,
  input  E22,
  input  E23,
  input  E24,
  input  E25,
  input  E26,
  input  E27,
  input  E28,
  input  E29,
  input  E30,
  input  E31,
  input  [4:0] in_33,
  output out_34
);

  wire mux16_1_out_21, mux16_2_out_21;

  MUX16 mux16_1 (
    .E0(E0), .E1(E1), .E2(E2), .E3(E3), .in_5(E4), .E5(E5), .E6(E6), .E7(E7), .E8(E8), .E9(E9), .E10(E10),
    .E11(E11), .in_13(E12), .E13(E13), .E14(E14), .E15(E15), .C(in_33[3]), .D(in_33[2]), .A(in_33[1]),
    .B(in_33[0]), .out_21(mux16_1_out_21));
  MUX16 mux16_2 (
    .E0(E16), .E1(E17), .E2(E18), .E3(E19), .in_5(E20), .E5(E21), .E6(E22), .E7(E23), .E8(E24), .E9(E25),
    .E10(E26), .E11(E27), .in_13(E28), .E13(E29), .E14(E30), .E15(E31), .C(in_33[3]), .D(in_33[2]),
    .A(in_33[1]), .B(in_33[0]), .out_21(mux16_2_out_21));
  MUX2 mux2_1 (.E0(mux16_1_out_21), .E1(mux16_2_out_21), .E(in_33[4]), .out_4(out_34));
endmodule

module MUX4 (
  input  in_1,
  input  in_2,
  input  in_3,
  input  in_4,
  input  in_5,
  input  in_6,
  output out_7
);

  wire and_1_out, and_2_out, and_3_out, and_4_out;

  and and_1 (and_1_out, in_1, ~in_5, ~in_6);  // AND_Gate
  and and_2 (and_2_out, in_2, ~in_5, in_6);  // AND_Gate
  and and_3 (and_3_out, in_3, in_5, ~in_6);  // AND_Gate
  and and_4 (and_4_out, in_4, in_5, in_6);
  or or_1 (out_7, and_1_out, and_2_out, and_3_out, and_4_out);
endmodule

module MUX16 (
  input  E0,
  input  E1,
  input  E2,
  input  E3,
  input  in_5,
  input  E5,
  input  E6,
  input  E7,
  input  E8,
  input  E9,
  input  E10,
  input  E11,
  input  in_13,
  input  E13,
  input  E14,
  input  E15,
  input  C,
  input  D,
  input  A,
  input  B,
  output out_21
);

  wire mux8_1_out_12, mux8_2_out_12;

  MUX8 mux8_1 (
    .E0(E0), .E1(E1), .E2(E2), .E3(E3), .E4(in_5), .E5(E5), .E6(E6), .E7(E7), .B(D), .C(A), .A(B),
    .out_12(mux8_1_out_12));
  MUX8 mux8_2 (
    .E0(E8), .E1(E9), .E2(E10), .E3(E11), .E4(in_13), .E5(E13), .E6(E14), .E7(E15), .B(D), .C(A), .A(B),
    .out_12(mux8_2_out_12));
  MUX2 mux2_1 (.E0(mux8_1_out_12), .E1(mux8_2_out_12), .E(C), .out_4(out_21));
endmodule

module MUX2 (
  input  E0,
  input  E1,
  input  E,
  output out_4
);

  wire and_1_out, and_2_out;

  and and_1 (and_1_out, E0, ~E);  // AND_Gate
  and and_2 (and_2_out, E1, E);
  or or_1 (out_4, and_1_out, and_2_out);
endmodule

module \CélulaULA  (
  input  A,
  input  B,
  input  Cin,
  input  [4:0] in_4,
  output Cout,
  output \Saída 
);

  wire and_1_out, nand_1_out, or_1_out, \somadorcompleto_1_saída_soma , xor_1_out;

  and and_1 (and_1_out, A, B);
  or or_1 (or_1_out, A, B);
  xor xor_1 (xor_1_out, A, B);
  somadorcompleto somadorcompleto_1 (
    .Cin(Cin), .A(A), .B(B), .\Saída_Soma (\somadorcompleto_1_saída_soma ), .Cout(Cout));
  nand nand_1 (nand_1_out, ~A, B);  // NAND_Gate
  MUX32 mux32_1 (
    .E0(and_1_out), .E1(or_1_out), .E2(\somadorcompleto_1_saída_soma ), .E3(xor_1_out), .E4(B), .E5(B),
    .E6(B), .E7(B), .E8(B), .E9(B), .E10(B), .E11(B), .E12(B), .E13(nand_1_out), .E14(nand_1_out),
    .E15(nand_1_out), .E16(nand_1_out), .E17(nand_1_out), .E18(nand_1_out), .E19(nand_1_out),
    .E20(nand_1_out), .E21(nand_1_out), .E22(nand_1_out), .E23(nand_1_out), .E24(nand_1_out),
    .E25(nand_1_out), .E26(nand_1_out), .E27(nand_1_out), .E28(nand_1_out), .E29(nand_1_out),
    .E30(nand_1_out), .E31(nand_1_out), .in_33(in_4), .out_34(\Saída ));
endmodule

module ULA (
  input  [31:0] A,
  input  [31:0] B,
  input  [4:0] OpCode,
  output out_4,
  output \SaídaDetector ,
  output [31:0] Resultado
);

  wire \célulaula_2_cout , \célulaula_3_cout , \célulaula_4_cout , \célulaula_5_cout , \célulaula_6_cout ,
       \célulaula_7_cout , \célulaula_8_cout , \célulaula_9_cout , \célulaula_10_cout , \célulaula_11_cout ,
       \célulaula_12_cout , \célulaula_13_cout , \célulaula_14_cout , \célulaula_15_cout ,
       \célulaula_16_cout , \célulaula_17_cout , \célulaula_18_cout , \célulaula_19_cout ,
       \célulaula_20_cout , \célulaula_21_cout , \célulaula_22_cout , \célulaula_23_cout ,
       \célulaula_24_cout , \célulaula_25_cout , \célulaula_26_cout , \célulaula_27_cout ,
       \célulaula_28_cout , \célulaula_29_cout , \célulaula_30_cout , \célulaula_31_cout ,
       \célulaula_32_cout , extra1detect_1_out_2, extra2detect_1_out_2, slldetect_1_out_2;
  wire [31:0] shiftleftlogico_1_out_3, shiftrightarit_1_out_3, shiftrightlogico_1_out_3;

  SLLDetect slldetect_1 (.in_1(OpCode), .out_2(slldetect_1_out_2));
  ShiftRightLogico shiftrightlogico_1 (
    .in_1(shiftleftlogico_1_out_3), .in_2(extra1detect_1_out_2), .out_3(shiftrightlogico_1_out_3));
  ShiftLeftLogico shiftleftlogico_1 (.in_1(B), .in_2(slldetect_1_out_2), .out_3(shiftleftlogico_1_out_3));
  extra2Detect extra2detect_1 (.in_1(OpCode), .out_2(extra2detect_1_out_2));
  extra1Detect extra1detect_1 (.in_1(OpCode), .out_2(extra1detect_1_out_2));
  ShiftRightArit shiftrightarit_1 (
    .in_1(shiftrightlogico_1_out_3), .Shift(extra2detect_1_out_2), .out_3(shiftrightarit_1_out_3));
  \CélulaULA  \célulaula_1  (
    .Cout(out_4), .Cin(\célulaula_2_cout ), .\Saída (Resultado[31]), .A(A[31]),
    .B(shiftrightarit_1_out_3[31]), .in_4(OpCode));
  \CélulaULA  \célulaula_2  (
    .Cout(\célulaula_2_cout ), .Cin(\célulaula_4_cout ), .\Saída (Resultado[30]), .A(A[30]),
    .B(shiftrightarit_1_out_3[30]), .in_4(OpCode));
  \CélulaULA  \célulaula_3  (
    .Cout(\célulaula_3_cout ), .Cin(\célulaula_5_cout ), .\Saída (Resultado[28]), .A(A[28]),
    .B(shiftrightarit_1_out_3[28]), .in_4(OpCode));
  \CélulaULA  \célulaula_4  (
    .Cout(\célulaula_4_cout ), .Cin(\célulaula_3_cout ), .\Saída (Resultado[29]), .A(A[29]),
    .B(shiftrightarit_1_out_3[29]), .in_4(OpCode));
  \CélulaULA  \célulaula_5  (
    .Cout(\célulaula_5_cout ), .Cin(\célulaula_6_cout ), .\Saída (Resultado[27]), .A(A[27]),
    .B(shiftrightarit_1_out_3[27]), .in_4(OpCode));
  \CélulaULA  \célulaula_6  (
    .Cout(\célulaula_6_cout ), .Cin(\célulaula_8_cout ), .\Saída (Resultado[26]), .A(A[26]),
    .B(shiftrightarit_1_out_3[26]), .in_4(OpCode));
  \CélulaULA  \célulaula_7  (
    .Cout(\célulaula_7_cout ), .Cin(\célulaula_9_cout ), .\Saída (Resultado[24]), .A(A[24]),
    .B(shiftrightarit_1_out_3[24]), .in_4(OpCode));
  \CélulaULA  \célulaula_8  (
    .Cout(\célulaula_8_cout ), .Cin(\célulaula_7_cout ), .\Saída (Resultado[25]), .A(A[25]),
    .B(shiftrightarit_1_out_3[25]), .in_4(OpCode));
  \CélulaULA  \célulaula_9  (
    .Cout(\célulaula_9_cout ), .Cin(\célulaula_10_cout ), .\Saída (Resultado[23]), .A(A[23]),
    .B(shiftrightarit_1_out_3[23]), .in_4(OpCode));
  \CélulaULA  \célulaula_10  (
    .Cout(\célulaula_10_cout ), .Cin(\célulaula_12_cout ), .\Saída (Resultado[22]), .A(A[22]),
    .B(shiftrightarit_1_out_3[22]), .in_4(OpCode));
  \CélulaULA  \célulaula_11  (
    .Cout(\célulaula_11_cout ), .Cin(\célulaula_13_cout ), .\Saída (Resultado[20]), .A(A[20]),
    .B(shiftrightarit_1_out_3[20]), .in_4(OpCode));
  \CélulaULA  \célulaula_12  (
    .Cout(\célulaula_12_cout ), .Cin(\célulaula_11_cout ), .\Saída (Resultado[21]), .A(A[21]),
    .B(shiftrightarit_1_out_3[21]), .in_4(OpCode));
  \CélulaULA  \célulaula_13  (
    .Cout(\célulaula_13_cout ), .Cin(\célulaula_14_cout ), .\Saída (Resultado[19]), .A(A[19]),
    .B(shiftrightarit_1_out_3[19]), .in_4(OpCode));
  \CélulaULA  \célulaula_14  (
    .Cout(\célulaula_14_cout ), .Cin(\célulaula_15_cout ), .\Saída (Resultado[18]), .A(A[18]),
    .B(shiftrightarit_1_out_3[18]), .in_4(OpCode));
  \CélulaULA  \célulaula_15  (
    .Cout(\célulaula_15_cout ), .Cin(\célulaula_16_cout ), .\Saída (Resultado[17]), .A(A[17]),
    .B(shiftrightarit_1_out_3[17]), .in_4(OpCode));
  \CélulaULA  \célulaula_16  (
    .Cout(\célulaula_16_cout ), .Cin(\célulaula_17_cout ), .\Saída (Resultado[16]), .A(A[16]),
    .B(shiftrightarit_1_out_3[16]), .in_4(OpCode));
  \CélulaULA  \célulaula_17  (
    .Cout(\célulaula_17_cout ), .Cin(\célulaula_18_cout ), .\Saída (Resultado[15]), .A(A[15]),
    .B(shiftrightarit_1_out_3[15]), .in_4(OpCode));
  \CélulaULA  \célulaula_18  (
    .Cout(\célulaula_18_cout ), .Cin(\célulaula_20_cout ), .\Saída (Resultado[14]), .A(A[14]),
    .B(shiftrightarit_1_out_3[14]), .in_4(OpCode));
  \CélulaULA  \célulaula_19  (
    .Cout(\célulaula_19_cout ), .Cin(\célulaula_21_cout ), .\Saída (Resultado[12]), .A(A[12]),
    .B(shiftrightarit_1_out_3[12]), .in_4(OpCode));
  \CélulaULA  \célulaula_20  (
    .Cout(\célulaula_20_cout ), .Cin(\célulaula_19_cout ), .\Saída (Resultado[13]), .A(A[13]),
    .B(shiftrightarit_1_out_3[13]), .in_4(OpCode));
  \CélulaULA  \célulaula_21  (
    .Cout(\célulaula_21_cout ), .Cin(\célulaula_22_cout ), .\Saída (Resultado[11]), .A(A[11]),
    .B(shiftrightarit_1_out_3[11]), .in_4(OpCode));
  \CélulaULA  \célulaula_22  (
    .Cout(\célulaula_22_cout ), .Cin(\célulaula_23_cout ), .\Saída (Resultado[10]), .A(A[10]),
    .B(shiftrightarit_1_out_3[10]), .in_4(OpCode));
  \CélulaULA  \célulaula_23  (
    .Cout(\célulaula_23_cout ), .Cin(\célulaula_24_cout ), .\Saída (Resultado[9]), .A(A[9]),
    .B(shiftrightarit_1_out_3[9]), .in_4(OpCode));
  \CélulaULA  \célulaula_24  (
    .Cout(\célulaula_24_cout ), .Cin(\célulaula_25_cout ), .\Saída (Resultado[8]), .A(A[8]),
    .B(shiftrightarit_1_out_3[8]), .in_4(OpCode));
  \CélulaULA  \célulaula_25  (
    .Cout(\célulaula_25_cout ), .Cin(\célulaula_26_cout ), .\Saída (Resultado[7]), .A(A[7]),
    .B(shiftrightarit_1_out_3[7]), .in_4(OpCode));
  \CélulaULA  \célulaula_26  (
    .Cout(\célulaula_26_cout ), .Cin(\célulaula_28_cout ), .\Saída (Resultado[6]), .A(A[6]),
    .B(shiftrightarit_1_out_3[6]), .in_4(OpCode));
  \CélulaULA  \célulaula_27  (
    .Cout(\célulaula_27_cout ), .Cin(\célulaula_30_cout ), .\Saída (Resultado[4]), .A(A[4]),
    .B(shiftrightarit_1_out_3[4]), .in_4(OpCode));
  \CélulaULA  \célulaula_28  (
    .Cout(\célulaula_28_cout ), .Cin(\célulaula_27_cout ), .\Saída (Resultado[5]), .A(A[5]),
    .B(shiftrightarit_1_out_3[5]), .in_4(OpCode));
  \CélulaULA  \célulaula_29  (
    .Cout(\célulaula_29_cout ), .Cin(\célulaula_31_cout ), .\Saída (Resultado[2]), .A(A[2]),
    .B(shiftrightarit_1_out_3[2]), .in_4(OpCode));
  \CélulaULA  \célulaula_30  (
    .Cout(\célulaula_30_cout ), .Cin(\célulaula_29_cout ), .\Saída (Resultado[3]), .A(A[3]),
    .B(shiftrightarit_1_out_3[3]), .in_4(OpCode));
  \CélulaULA  \célulaula_31  (
    .Cout(\célulaula_31_cout ), .Cin(\célulaula_32_cout ), .\Saída (Resultado[1]), .A(A[1]),
    .B(shiftrightarit_1_out_3[1]), .in_4(OpCode));
  \CélulaULA  \célulaula_32  (
    .Cout(\célulaula_32_cout ), .Cin(1'b0), .\Saída (Resultado[0]), .A(A[0]), .B(shiftrightarit_1_out_3[0]),
    .in_4(OpCode));
  nor nor_1 (\SaídaDetector , Resultado[0], Resultado[1], Resultado[2], Resultado[3], Resultado[4], Resultado[5], Resultado[6], Resultado[7], Resultado[8], Resultado[9], Resultado[10], Resultado[11], Resultado[12], Resultado[13], Resultado[14], Resultado[15], Resultado[16], Resultado[17], Resultado[18], Resultado[19], Resultado[20], Resultado[21], Resultado[22], Resultado[23], Resultado[24], Resultado[25], Resultado[26], Resultado[27], Resultado[28], Resultado[29], Resultado[30], Resultado[31]);
endmodule

module MUX8 (
  input  E0,
  input  E1,
  input  E2,
  input  E3,
  input  E4,
  input  E5,
  input  E6,
  input  E7,
  input  B,
  input  C,
  input  A,
  output out_12
);

  wire mux4_1_out_7, mux4_2_out_7;

  MUX4 mux4_1 (.in_1(E0), .in_2(E1), .in_3(E2), .in_4(E3), .in_5(C), .in_6(A), .out_7(mux4_1_out_7));
  MUX4 mux4_2 (.in_1(E4), .in_2(E5), .in_3(E6), .in_4(E7), .in_5(C), .in_6(A), .out_7(mux4_2_out_7));
  MUX2 mux2_1 (.E0(mux4_1_out_7), .E1(mux4_2_out_7), .E(B), .out_4(out_12));
endmodule

module ShiftLeftLogico (
  input  [31:0] in_1,
  input  in_2,
  output [31:0] out_3
);

  MUX2maisbits mux2maisbits_1 (.E0(in_1), .E1({in_1[30:0], 1'b0}), .E(in_2), .out_4(out_3));
endmodule

module MUX2maisbits (
  input  [31:0] E0,
  input  [31:0] E1,
  input  E,
  output [31:0] out_4
);

  wire [31:0] and_1_out, and_2_out;

  assign and_1_out = E0 & ~{32{E}};  // AND_Gate and_1, 32 bits wide
  assign and_2_out = E1 & {32{E}};  // AND_Gate and_2, 32 bits wide
  assign out_4 = and_1_out | and_2_out;  // OR_Gate or_1, 32 bits wide
endmodule

module ShiftRightLogico (
  input  [31:0] in_1,
  input  in_2,
  output [31:0] out_3
);

  MUX2maisbits mux2maisbits_1 (.E0(in_1), .E1({1'b0, in_1[31:1]}), .E(in_2), .out_4(out_3));
endmodule

module ShiftRightArit (
  input  [31:0] in_1,
  input  Shift,
  output [31:0] out_3
);

  MUX2maisbits mux2maisbits_1 (.E0(in_1), .E1({{2{in_1[31]}}, in_1[30:1]}), .E(Shift), .out_4(out_3));
endmodule

module ShiftLeftArit (
  input  [31:0] in_1,
  input  in_2,
  output [31:0] out_3
);

  MUX2maisbits mux2maisbits_1 (.E0(in_1), .E1({in_1[30:0], in_1[0]}), .E(in_2), .out_4(out_3));
endmodule

module SLLDetect (
  input  [4:0] in_1,
  output out_2
);

  and and_1 (out_2, ~in_1[0], ~in_1[1], in_1[2], ~in_1[3], ~in_1[4]);  // AND_Gate

  // Notes on the sheet:
  //   00000 = and
  //   00001 = or
  //   00010 = soma
  //   00011 = xor
  //   00100 = sll
endmodule

module ANDDetect (
  input  [4:0] in_1,
  output out_2
);

  and and_1 (out_2, ~in_1[0], ~in_1[1], ~in_1[2], ~in_1[3], ~in_1[4]);  // AND_Gate
endmodule

module ORDetect (
  input  [4:0] in_1,
  output out_2
);

  and and_1 (out_2, in_1[0], ~in_1[1], ~in_1[2], ~in_1[3], ~in_1[4]);  // AND_Gate
endmodule

module SOMADetect (
  input  [4:0] in_1,
  output out_2
);

  and and_1 (out_2, ~in_1[0], in_1[1], ~in_1[2], ~in_1[3], ~in_1[4]);  // AND_Gate
endmodule

module XORDETECT (
  input  [4:0] in_1,
  output out_2
);

  and and_1 (out_2, in_1[0], in_1[1], ~in_1[2], ~in_1[3], ~in_1[4]);  // AND_Gate
endmodule

module extra1Detect (
  input  [4:0] in_1,
  output out_2
);

  and and_1 (out_2, in_1[0], ~in_1[1], in_1[2], ~in_1[3], ~in_1[4]);  // AND_Gate
endmodule

module extra2Detect (
  input  [4:0] in_1,
  output out_2
);

  and and_1 (out_2, ~in_1[0], in_1[1], in_1[2], ~in_1[3], ~in_1[4]);  // AND_Gate
endmodule

module extra3Detect (
  input  [4:0] in_1,
  output out_2
);

  and and_1 (out_2, in_1[0], in_1[1], in_1[2], ~in_1[3], ~in_1[4]);  // AND_Gate
endmodule

module extra4Detect (
  input  [4:0] in_1,
  output out_2
);

  and and_1 (out_2, ~in_1[0], ~in_1[1], ~in_1[2], in_1[3], ~in_1[4]);  // AND_Gate
endmodule

module extra5Detect (
  input  [4:0] in_1,
  output out_2
);

  and and_1 (out_2, in_1[0], ~in_1[1], ~in_1[2], in_1[3], ~in_1[4]);  // AND_Gate
endmodule

module extra6Detect (
  input  [4:0] in_1,
  output out_2
);

  and and_1 (out_2, ~in_1[0], in_1[1], ~in_1[2], in_1[3], ~in_1[4]);  // AND_Gate
endmodule

module extra7Detecy (
  input  [4:0] in_1,
  output out_2
);

  and and_1 (out_2, in_1[0], in_1[1], ~in_1[2], in_1[3], ~in_1[4]);  // AND_Gate
endmodule

module extra8Detect (
  input  [4:0] in_1,
  output out_2
);

  and and_1 (out_2, ~in_1[0], ~in_1[1], in_1[2], in_1[3], ~in_1[4]);  // AND_Gate
endmodule

module extra9Detect (
  input  [4:0] in_1,
  output out_2
);

  and and_1 (out_2, in_1[0], ~in_1[1], in_1[2], in_1[3], ~in_1[4]);  // AND_Gate
endmodule

module extra10Detect (
  input  [4:0] in_1,
  output out_2
);

  and and_1 (out_2, ~in_1[0], in_1[1], in_1[2], in_1[3], ~in_1[4]);  // AND_Gate
endmodule

module extra11Detect (
  input  [4:0] in_1,
  output out_2
);

  and and_1 (out_2, in_1[0], in_1[1], in_1[2], in_1[3], ~in_1[4]);  // AND_Gate
endmodule

module Registrador32bits (
  input  [31:0] DataIN,
  input  Save,
  input  Reset,
  output [31:0] DataOUT
);

  D_Flip_Flop d_ff_1 (.clk(Save), .D(DataIN[31]), .Q(DataOUT[31]), .reset(Reset));  // open: Qn, preset, en
  D_Flip_Flop d_ff_2 (.clk(Save), .D(DataIN[30]), .Q(DataOUT[30]), .reset(Reset));  // open: Qn, preset, en
  D_Flip_Flop d_ff_3 (.clk(Save), .D(DataIN[29]), .Q(DataOUT[29]), .reset(Reset));  // open: Qn, preset, en
  D_Flip_Flop d_ff_4 (.clk(Save), .D(DataIN[28]), .Q(DataOUT[28]), .reset(Reset));  // open: Qn, preset, en
  D_Flip_Flop d_ff_5 (.clk(Save), .D(DataIN[27]), .Q(DataOUT[27]), .reset(Reset));  // open: Qn, preset, en
  D_Flip_Flop d_ff_6 (.clk(Save), .D(DataIN[26]), .Q(DataOUT[26]), .reset(Reset));  // open: Qn, preset, en
  D_Flip_Flop d_ff_7 (.clk(Save), .D(DataIN[25]), .Q(DataOUT[25]), .reset(Reset));  // open: Qn, preset, en
  D_Flip_Flop d_ff_8 (.clk(Save), .D(DataIN[24]), .Q(DataOUT[24]), .reset(Reset));  // open: Qn, preset, en
  D_Flip_Flop d_ff_9 (.clk(Save), .D(DataIN[23]), .Q(DataOUT[23]), .reset(Reset));  // open: Qn, preset, en
  D_Flip_Flop d_ff_10 (.clk(Save), .D(DataIN[22]), .Q(DataOUT[22]), .reset(Reset));  // open: Qn, preset, en
  D_Flip_Flop d_ff_11 (.clk(Save), .D(DataIN[21]), .Q(DataOUT[21]), .reset(Reset));  // open: Qn, preset, en
  D_Flip_Flop d_ff_12 (.clk(Save), .D(DataIN[20]), .Q(DataOUT[20]), .reset(Reset));  // open: Qn, preset, en
  D_Flip_Flop d_ff_13 (.clk(Save), .D(DataIN[19]), .Q(DataOUT[19]), .reset(Reset));  // open: Qn, preset, en
  D_Flip_Flop d_ff_14 (.clk(Save), .D(DataIN[18]), .Q(DataOUT[18]), .reset(Reset));  // open: Qn, preset, en
  D_Flip_Flop d_ff_15 (.clk(Save), .D(DataIN[17]), .Q(DataOUT[17]), .reset(Reset));  // open: Qn, preset, en
  D_Flip_Flop d_ff_16 (.clk(Save), .D(DataIN[16]), .Q(DataOUT[16]), .reset(Reset));  // open: Qn, preset, en
  D_Flip_Flop d_ff_17 (.clk(Save), .D(DataIN[15]), .Q(DataOUT[15]), .reset(Reset));  // open: Qn, preset, en
  D_Flip_Flop d_ff_18 (.clk(Save), .D(DataIN[14]), .Q(DataOUT[14]), .reset(Reset));  // open: Qn, preset, en
  D_Flip_Flop d_ff_19 (.clk(Save), .D(DataIN[13]), .Q(DataOUT[13]), .reset(Reset));  // open: Qn, preset, en
  D_Flip_Flop d_ff_20 (.clk(Save), .D(DataIN[12]), .Q(DataOUT[12]), .reset(Reset));  // open: Qn, preset, en
  D_Flip_Flop d_ff_21 (.clk(Save), .D(DataIN[11]), .Q(DataOUT[11]), .reset(Reset));  // open: Qn, preset, en
  D_Flip_Flop d_ff_22 (.clk(Save), .D(DataIN[10]), .Q(DataOUT[10]), .reset(Reset));  // open: Qn, preset, en
  D_Flip_Flop d_ff_23 (.clk(Save), .D(DataIN[9]), .Q(DataOUT[9]), .reset(Reset));  // open: Qn, preset, en
  D_Flip_Flop d_ff_24 (.clk(Save), .D(DataIN[8]), .Q(DataOUT[8]), .reset(Reset));  // open: Qn, preset, en
  D_Flip_Flop d_ff_25 (.clk(Save), .D(DataIN[7]), .Q(DataOUT[7]), .reset(Reset));  // open: Qn, preset, en
  D_Flip_Flop d_ff_26 (.clk(Save), .D(DataIN[6]), .Q(DataOUT[6]), .reset(Reset));  // open: Qn, preset, en
  D_Flip_Flop d_ff_27 (.clk(Save), .D(DataIN[5]), .Q(DataOUT[5]), .reset(Reset));  // open: Qn, preset, en
  D_Flip_Flop d_ff_28 (.clk(Save), .D(DataIN[4]), .Q(DataOUT[4]), .reset(Reset));  // open: Qn, preset, en
  D_Flip_Flop d_ff_29 (.clk(Save), .D(DataIN[3]), .Q(DataOUT[3]), .reset(Reset));  // open: Qn, preset, en
  D_Flip_Flop d_ff_30 (.clk(Save), .D(DataIN[2]), .Q(DataOUT[2]), .reset(Reset));  // open: Qn, preset, en
  D_Flip_Flop d_ff_31 (.clk(Save), .D(DataIN[1]), .Q(DataOUT[1]), .reset(Reset));  // open: Qn, preset, en
  D_Flip_Flop d_ff_32 (.clk(Save), .D(DataIN[0]), .Q(DataOUT[0]), .reset(Reset));  // open: Qn, preset, en
endmodule

module BancoRegistrador32bits (
  input  [31:0] DataIN,
  input  Reset,
  input  [4:0] RegistradorA,
  input  Clock,
  input  [4:0] RegistradorB,
  input  [4:0] RegWrite,
  output [31:0] A,
  output [31:0] B
);

  wire demultiplexer_1_out0, demultiplexer_1_out1, demultiplexer_1_out2, demultiplexer_1_out3,
       demultiplexer_1_out4, demultiplexer_1_out5, demultiplexer_1_out6, demultiplexer_1_out7,
       demultiplexer_1_out8, demultiplexer_1_out9, demultiplexer_1_out10, demultiplexer_1_out11,
       demultiplexer_1_out12, demultiplexer_1_out13, demultiplexer_1_out14, demultiplexer_1_out15,
       demultiplexer_1_out16, demultiplexer_1_out17, demultiplexer_1_out18, demultiplexer_1_out19,
       demultiplexer_1_out20, demultiplexer_1_out21, demultiplexer_1_out22, demultiplexer_1_out23,
       demultiplexer_1_out24, demultiplexer_1_out25, demultiplexer_1_out26, demultiplexer_1_out27,
       demultiplexer_1_out28, demultiplexer_1_out29, demultiplexer_1_out30, demultiplexer_1_out31;
  wire [31:0] registrador32bits_1_dataout, registrador32bits_2_dataout, registrador32bits_3_dataout,
       registrador32bits_4_dataout, registrador32bits_5_dataout, registrador32bits_6_dataout,
       registrador32bits_7_dataout, registrador32bits_8_dataout, registrador32bits_9_dataout,
       registrador32bits_10_dataout, registrador32bits_11_dataout, registrador32bits_12_dataout,
       registrador32bits_13_dataout, registrador32bits_14_dataout, registrador32bits_15_dataout,
       registrador32bits_16_dataout, registrador32bits_17_dataout, registrador32bits_18_dataout,
       registrador32bits_19_dataout, registrador32bits_20_dataout, registrador32bits_21_dataout,
       registrador32bits_22_dataout, registrador32bits_23_dataout, registrador32bits_24_dataout,
       registrador32bits_25_dataout, registrador32bits_26_dataout, registrador32bits_27_dataout,
       registrador32bits_28_dataout, registrador32bits_29_dataout, registrador32bits_30_dataout,
       registrador32bits_31_dataout, registrador32bits_32_dataout;

  Demultiplexer #(.select(5), .enable("false")) demultiplexer_1 (
    .out0(demultiplexer_1_out0), .out1(demultiplexer_1_out1), .out2(demultiplexer_1_out2),
    .out3(demultiplexer_1_out3), .out4(demultiplexer_1_out4), .out5(demultiplexer_1_out5),
    .out6(demultiplexer_1_out6), .out7(demultiplexer_1_out7), .out8(demultiplexer_1_out8),
    .out9(demultiplexer_1_out9), .out10(demultiplexer_1_out10), .out11(demultiplexer_1_out11),
    .out12(demultiplexer_1_out12), .out13(demultiplexer_1_out13), .out14(demultiplexer_1_out14),
    .out15(demultiplexer_1_out15), .out16(demultiplexer_1_out16), .out17(demultiplexer_1_out17),
    .out18(demultiplexer_1_out18), .out19(demultiplexer_1_out19), .out20(demultiplexer_1_out20),
    .out21(demultiplexer_1_out21), .out22(demultiplexer_1_out22), .out23(demultiplexer_1_out23),
    .out24(demultiplexer_1_out24), .out25(demultiplexer_1_out25), .out26(demultiplexer_1_out26),
    .out27(demultiplexer_1_out27), .out28(demultiplexer_1_out28), .out29(demultiplexer_1_out29),
    .out30(demultiplexer_1_out30), .out31(demultiplexer_1_out31), .in(Clock), .sel(RegWrite));
  Registrador32bits registrador32bits_1 (
    .DataIN(DataIN), .Save(demultiplexer_1_out0), .Reset(Reset), .DataOUT(registrador32bits_1_dataout));
  Registrador32bits registrador32bits_2 (
    .DataIN(DataIN), .Save(demultiplexer_1_out1), .Reset(Reset), .DataOUT(registrador32bits_2_dataout));
  Registrador32bits registrador32bits_3 (
    .DataIN(DataIN), .Save(demultiplexer_1_out2), .Reset(Reset), .DataOUT(registrador32bits_3_dataout));
  Registrador32bits registrador32bits_4 (
    .DataIN(DataIN), .Save(demultiplexer_1_out3), .Reset(Reset), .DataOUT(registrador32bits_4_dataout));
  Registrador32bits registrador32bits_5 (
    .DataIN(DataIN), .Save(demultiplexer_1_out4), .Reset(Reset), .DataOUT(registrador32bits_5_dataout));
  Registrador32bits registrador32bits_6 (
    .DataIN(DataIN), .Save(demultiplexer_1_out5), .Reset(Reset), .DataOUT(registrador32bits_6_dataout));
  Registrador32bits registrador32bits_7 (
    .DataIN(DataIN), .Save(demultiplexer_1_out6), .Reset(Reset), .DataOUT(registrador32bits_7_dataout));
  Registrador32bits registrador32bits_8 (
    .DataIN(DataIN), .Save(demultiplexer_1_out7), .Reset(Reset), .DataOUT(registrador32bits_8_dataout));
  Registrador32bits registrador32bits_9 (
    .DataIN(DataIN), .Save(demultiplexer_1_out8), .Reset(Reset), .DataOUT(registrador32bits_9_dataout));
  Registrador32bits registrador32bits_10 (
    .DataIN(DataIN), .Save(demultiplexer_1_out9), .Reset(Reset), .DataOUT(registrador32bits_10_dataout));
  Registrador32bits registrador32bits_11 (
    .DataIN(DataIN), .Save(demultiplexer_1_out10), .Reset(Reset), .DataOUT(registrador32bits_11_dataout));
  Registrador32bits registrador32bits_12 (
    .DataIN(DataIN), .Save(demultiplexer_1_out11), .Reset(Reset), .DataOUT(registrador32bits_12_dataout));
  Registrador32bits registrador32bits_13 (
    .Save(demultiplexer_1_out12), .Reset(Reset), .DataOUT(registrador32bits_13_dataout));  // open: DataIN
  Registrador32bits registrador32bits_14 (
    .DataIN(DataIN), .Save(demultiplexer_1_out13), .Reset(Reset), .DataOUT(registrador32bits_14_dataout));
  Registrador32bits registrador32bits_15 (
    .DataIN(DataIN), .Save(demultiplexer_1_out14), .Reset(Reset), .DataOUT(registrador32bits_15_dataout));
  Registrador32bits registrador32bits_16 (
    .DataIN(DataIN), .Save(demultiplexer_1_out15), .Reset(Reset), .DataOUT(registrador32bits_16_dataout));
  Registrador32bits registrador32bits_17 (
    .DataIN(DataIN), .Save(demultiplexer_1_out16), .Reset(Reset), .DataOUT(registrador32bits_17_dataout));
  Registrador32bits registrador32bits_18 (
    .DataIN(DataIN), .Save(demultiplexer_1_out17), .Reset(Reset), .DataOUT(registrador32bits_18_dataout));
  Registrador32bits registrador32bits_19 (
    .DataIN(DataIN), .Save(demultiplexer_1_out18), .Reset(Reset), .DataOUT(registrador32bits_19_dataout));
  Registrador32bits registrador32bits_20 (
    .DataIN(DataIN), .Save(demultiplexer_1_out19), .Reset(Reset), .DataOUT(registrador32bits_20_dataout));
  Registrador32bits registrador32bits_21 (
    .DataIN(DataIN), .Save(demultiplexer_1_out20), .Reset(Reset), .DataOUT(registrador32bits_21_dataout));
  Registrador32bits registrador32bits_22 (
    .DataIN(DataIN), .Save(demultiplexer_1_out21), .Reset(Reset), .DataOUT(registrador32bits_22_dataout));
  Registrador32bits registrador32bits_23 (
    .DataIN(DataIN), .Save(demultiplexer_1_out22), .Reset(Reset), .DataOUT(registrador32bits_23_dataout));
  Registrador32bits registrador32bits_24 (
    .DataIN(DataIN), .Save(demultiplexer_1_out23), .Reset(Reset), .DataOUT(registrador32bits_24_dataout));
  Registrador32bits registrador32bits_25 (
    .DataIN(DataIN), .Save(demultiplexer_1_out24), .Reset(Reset), .DataOUT(registrador32bits_25_dataout));
  Registrador32bits registrador32bits_26 (
    .DataIN(DataIN), .Save(demultiplexer_1_out25), .Reset(Reset), .DataOUT(registrador32bits_26_dataout));
  Registrador32bits registrador32bits_27 (
    .DataIN(DataIN), .Save(demultiplexer_1_out26), .Reset(Reset), .DataOUT(registrador32bits_27_dataout));
  Registrador32bits registrador32bits_28 (
    .DataIN(DataIN), .Save(demultiplexer_1_out27), .Reset(Reset), .DataOUT(registrador32bits_28_dataout));
  Registrador32bits registrador32bits_29 (
    .DataIN(DataIN), .Save(demultiplexer_1_out28), .Reset(Reset), .DataOUT(registrador32bits_29_dataout));
  Registrador32bits registrador32bits_30 (
    .DataIN(DataIN), .Save(demultiplexer_1_out29), .Reset(Reset), .DataOUT(registrador32bits_30_dataout));
  Registrador32bits registrador32bits_31 (
    .DataIN(DataIN), .Save(demultiplexer_1_out30), .Reset(Reset), .DataOUT(registrador32bits_31_dataout));
  Registrador32bits registrador32bits_32 (
    .DataIN(DataIN), .Save(demultiplexer_1_out31), .Reset(Reset), .DataOUT(registrador32bits_32_dataout));
  Multiplexer #(.select(5), .width(32), .enable("false")) multiplexer_1 (
    .in0(registrador32bits_1_dataout), .in1(registrador32bits_2_dataout), .in2(registrador32bits_3_dataout),
    .in3(registrador32bits_4_dataout), .in4(registrador32bits_5_dataout), .in5(registrador32bits_6_dataout),
    .in6(registrador32bits_7_dataout), .in7(registrador32bits_8_dataout), .in8(registrador32bits_9_dataout),
    .in9(registrador32bits_10_dataout), .in10(registrador32bits_11_dataout),
    .in11(registrador32bits_12_dataout), .in12(registrador32bits_13_dataout),
    .in13(registrador32bits_14_dataout), .in14(registrador32bits_15_dataout),
    .in15(registrador32bits_16_dataout), .in16(registrador32bits_17_dataout),
    .in17(registrador32bits_18_dataout), .in18(registrador32bits_19_dataout),
    .in19(registrador32bits_20_dataout), .in20(registrador32bits_21_dataout),
    .in21(registrador32bits_22_dataout), .in22(registrador32bits_23_dataout),
    .in23(registrador32bits_24_dataout), .in24(registrador32bits_25_dataout),
    .in25(registrador32bits_26_dataout), .in26(registrador32bits_27_dataout),
    .in27(registrador32bits_28_dataout), .in28(registrador32bits_29_dataout),
    .in29(registrador32bits_30_dataout), .in30(registrador32bits_31_dataout),
    .in31(registrador32bits_32_dataout), .out(A), .sel(RegistradorA));
  Multiplexer #(.select(5), .width(32), .enable("false")) multiplexer_2 (
    .in0(registrador32bits_1_dataout), .in1(registrador32bits_2_dataout), .in2(registrador32bits_3_dataout),
    .in3(registrador32bits_4_dataout), .in4(registrador32bits_5_dataout), .in5(registrador32bits_6_dataout),
    .in6(registrador32bits_7_dataout), .in7(registrador32bits_8_dataout), .in8(registrador32bits_9_dataout),
    .in9(registrador32bits_10_dataout), .in10(registrador32bits_11_dataout),
    .in11(registrador32bits_12_dataout), .in12(registrador32bits_13_dataout),
    .in13(registrador32bits_14_dataout), .in14(registrador32bits_15_dataout),
    .in15(registrador32bits_16_dataout), .in16(registrador32bits_17_dataout),
    .in17(registrador32bits_18_dataout), .in18(registrador32bits_19_dataout),
    .in19(registrador32bits_20_dataout), .in20(registrador32bits_21_dataout),
    .in21(registrador32bits_22_dataout), .in22(registrador32bits_23_dataout),
    .in23(registrador32bits_24_dataout), .in24(registrador32bits_25_dataout),
    .in25(registrador32bits_26_dataout), .in26(registrador32bits_27_dataout),
    .in27(registrador32bits_28_dataout), .in28(registrador32bits_29_dataout),
    .in29(registrador32bits_30_dataout), .in30(registrador32bits_31_dataout),
    .in31(registrador32bits_32_dataout), .out(B), .sel(RegistradorB));
endmodule

module \Avaliação2  (
  input  [31:0] in_1,
  input  Reset,
  input  CLK,
  input  Contexto,
  input  [4:0] RegW,
  input  [4:0] RegB,
  input  [4:0] RegA,
  output [31:0] out_8,
  output [31:0] out_9
);

  wire demultiplexer_1_out0, demultiplexer_1_out1;
  wire [31:0] bancoregistrador32bits_1_a, bancoregistrador32bits_1_b, bancoregistrador32bits_2_a,
       bancoregistrador32bits_2_b;

  Demultiplexer #(.enable("false")) demultiplexer_1 (
    .out0(demultiplexer_1_out0), .out1(demultiplexer_1_out1), .in(CLK), .sel(Contexto));
  BancoRegistrador32bits bancoregistrador32bits_1 (
    .Reset(Reset), .Clock(demultiplexer_1_out0), .DataIN(in_1), .RegWrite(RegW), .RegistradorB(RegB),
    .RegistradorA(RegA), .A(bancoregistrador32bits_1_a), .B(bancoregistrador32bits_1_b));
  BancoRegistrador32bits bancoregistrador32bits_2 (
    .Reset(Reset), .Clock(demultiplexer_1_out1), .DataIN(in_1), .RegWrite(RegW), .RegistradorB(RegB),
    .RegistradorA(RegA), .A(bancoregistrador32bits_2_a), .B(bancoregistrador32bits_2_b));
  Multiplexer #(.width(32), .enable("false")) multiplexer_1 (
    .in0(bancoregistrador32bits_1_a), .in1(bancoregistrador32bits_2_a), .out(out_8), .sel(Contexto));
  Multiplexer #(.width(32), .enable("false")) multiplexer_2 (
    .in0(bancoregistrador32bits_1_b), .in1(bancoregistrador32bits_2_b), .out(out_9), .sel(Contexto));
endmodule

module ViaDeDados (
  input  Clock,
  input  Reset,
  output out_3,
  output [31:0] out_4
);

  wire not_1_out;
  wire [7:0] adder_1_out, register_1_q;
  wire [31:0] bancoregistrador32bits_1_a, bancoregistrador32bits_1_b, ext_1_out_2, multiplexer_1_out,
       ula_1_resultado;

  not not_1 (not_1_out, Clock);
  Adder adder_1 (.a(register_1_q), .b(8'h1), .out(adder_1_out));  // open: cin, cout
  Register register_1 (.D(adder_1_out), .Q(register_1_q), .clk(not_1_out), .clr(Reset));  // open: en
  RAM #(.dataWidth(32)) ram_1 (.addr(register_1_q), .data(out_4));  // open: sel, clk, ld, clr
  BancoRegistrador32bits bancoregistrador32bits_1 (
    .Reset(Reset), .Clock(Clock), .DataIN(ula_1_resultado), .RegWrite(out_4[26:22]),
    .RegistradorB(out_4[21:17]), .RegistradorA(out_4[16:12]), .A(bancoregistrador32bits_1_a),
    .B(bancoregistrador32bits_1_b));
  Multiplexer #(.width(32), .enable("false")) multiplexer_1 (
    .in0(bancoregistrador32bits_1_b), .in1(ext_1_out_2), .out(multiplexer_1_out), .sel(out_4[0]));
  ULA ula_1 (
    .A(bancoregistrador32bits_1_a), .B(multiplexer_1_out), .OpCode(out_4[31:27]), .\SaídaDetector (out_3),
    .Resultado(ula_1_resultado));  // open: out_4
  ext ext_1 (.out_2(ext_1_out_2), .in_1(out_4[11:1]));
endmodule

module ext (
  input  [10:0] in_1,
  output [31:0] out_2
);


  assign out_2 = {{22{in_1[10]}}, in_1[9:0]};
endmodule
