// Logisim project teste.circ as structural Verilog
module main (
  input  in_1,
  input  in_2,
  output out_3,
  output out_4
);

  and and_1 (out_3, in_1, in_2);
  or or_1 (out_4, in_1, in_2);
endmodule

module mux2 (
  input  A,
  input  B,
  input  in_3,
  output out_4
);

  wire and_1_out, and_2_out;

  and and_1 (and_1_out, A, ~in_3);  // AND_Gate
  and and_2 (and_2_out, B, in_3);
  or or_1 (out_4, and_1_out, and_2_out);
endmodule

module MUX4 (
  input  A,
  input  B,
  input  C,
  input  D,
  input  in_5,
  input  in_6,
  output out_7
);

  wire mux2_1_out_4, mux2_2_out_4;

  mux2 mux2_1 (.A(A), .B(B), .in_3(in_6), .out_4(mux2_1_out_4));
  mux2 mux2_2 (.A(C), .B(D), .in_3(in_6), .out_4(mux2_2_out_4));
  mux2 mux2_3 (.A(mux2_1_out_4), .B(mux2_2_out_4), .in_3(in_5), .out_4(out_7));
endmodule

module mux4b (
  input  in_1,
  input  in_2,
  input  in_3,
  input  in_4,
  input  [1:0] in_5,
  output out_6
);

  wire and_1_out, and_2_out, and_3_out, and_4_out;

  and and_1 (and_1_out, in_1, ~in_5[1], ~in_5[0]);  // AND_Gate
  and and_2 (and_2_out, in_2, ~in_5[1], in_5[0]);  // AND_Gate
  and and_3 (and_3_out, in_3, in_5[1], ~in_5[0]);  // AND_Gate
  and and_4 (and_4_out, in_4, in_5[1], in_5[0]);
  or or_1 (out_6, and_1_out, and_2_out, and_3_out, and_4_out);
endmodule

module mux32 (
  input  E,
  input  D,
  input  C,
  input  B,
  input  A,
  output out_6
);

  wire mux16_1_out_21, mux16_2_out_21, undriven, undriven_2, undriven_3, undriven_4, undriven_5, undriven_6,
       undriven_7, undriven_8, undriven_9, undriven_10, undriven_11, undriven_12, undriven_13, undriven_14,
       undriven_15, undriven_16, undriven_17, undriven_18, undriven_19, undriven_20, undriven_21,
       undriven_22, undriven_23, undriven_24, undriven_25, undriven_26, undriven_27, undriven_28,
       undriven_29, undriven_30;

  mux16 mux16_1 (
    .in_1(undriven), .in_2(undriven_2), .in_3(undriven_3), .in_4(undriven_4), .in_5(undriven_5),
    .in_6(undriven_6), .in_7(undriven_7), .in_8(undriven_8), .in_9(undriven_9), .in_10(undriven_27),
    .in_11(undriven_27), .in_12(undriven_10), .in_13(undriven_28), .in_14(undriven_11), .in_15(undriven_12),
    .in_16(undriven_29), .C(C), .D(B), .A(A), .B(D), .out_21(mux16_1_out_21));
  mux16 mux16_2 (
    .in_1(undriven_13), .in_2(undriven_14), .in_3(undriven_15), .in_4(undriven_16), .in_5(undriven_17),
    .in_6(undriven_18), .in_7(undriven_19), .in_8(undriven_20), .in_9(undriven_21), .in_10(undriven_22),
    .in_11(undriven_22), .in_12(undriven_23), .in_13(undriven_24), .in_14(undriven_25), .in_15(undriven_26),
    .in_16(undriven_30), .C(E), .D(B), .A(C), .B(D), .out_21(mux16_2_out_21));
  mux2 mux2_1 (.A(mux16_1_out_21), .B(mux16_2_out_21), .in_3(E), .out_4(out_6));
endmodule

module mux16 (
  input  in_1,
  input  in_2,
  input  in_3,
  input  in_4,
  input  in_5,
  input  in_6,
  input  in_7,
  input  in_8,
  input  in_9,
  input  in_10,
  input  in_11,
  input  in_12,
  input  in_13,
  input  in_14,
  input  in_15,
  input  in_16,
  input  C,
  input  D,
  input  A,
  input  B,
  output out_21
);

  wire mux4_1_out_7, mux4_2_out_7, mux4_3_out_7, mux4_4_out_7;

  MUX4 mux4_1 (.A(in_1), .B(in_2), .C(in_3), .D(in_4), .in_5(C), .in_6(D), .out_7(mux4_1_out_7));
  MUX4 mux4_2 (.A(in_5), .B(in_6), .C(in_7), .D(in_8), .in_5(C), .in_6(D), .out_7(mux4_2_out_7));
  MUX4 mux4_3 (.A(in_9), .B(in_10), .C(in_11), .D(in_12), .in_5(C), .in_6(D), .out_7(mux4_3_out_7));
  MUX4 mux4_4 (.A(in_13), .B(in_14), .C(in_15), .D(in_15), .in_5(C), .in_6(D), .out_7(mux4_4_out_7));
  MUX4 mux4_5 (
    .A(mux4_1_out_7), .B(mux4_2_out_7), .C(mux4_3_out_7), .D(mux4_4_out_7), .in_5(A), .in_6(B), .out_7(out_21));

  assign in_16 = in_15;
endmodule

module mux8 (
  input  in_1,
  input  in_2,
  input  in_3,
  input  in_4,
  input  in_5,
  input  in_6,
  input  in_7,
  input  in_8,
  input  in_9,
  input  in_10,
  input  in_11
);

  wire mux4b_1_out_6, mux4b_2_out_6;

  mux4b mux4b_1 (.in_1(in_1), .in_2(in_2), .in_3(in_3), .in_4(in_4), .out_6(mux4b_1_out_6));  // open: in_5
  mux4b mux4b_2 (.in_1(in_5), .in_2(in_6), .in_3(in_7), .in_4(in_8), .out_6(mux4b_2_out_6));  // open: in_5
endmodule

module somador_de_ckt1 (
  input  in_1,
  input  in_2
);
endmodule

module ULACelula (
  input  in_1,
  input  in_2
);

  // AND_Gate and_1 has open pins: in0=in_1, in1=in_2, out=open
  // OR_Gate or_1 has open pins: in0=in_1, in1=in_2, out=open
endmodule

module ShiftRightLogico (
  input  [3:0] in_1
);

  // Pins of 3 and 4 bits meet at in_1
endmodule
